# Fritzing sketch 13.002.00.01.50 (saved by Fritzing 0.3.14b)
breadboards: 3

parts:
  DI1 = 7-Segment LED Display [package=THT]
  DI2 = 7-Segment LED Display [package=THT]  # not connected
  DI3 = 7-Segment LED Display [package=THT]  # not connected
  DI4 = 7-Segment LED Display [package=THT]  # not connected
  R201 = Resistor [resistance=68 package=THT]
  R201_2 = Resistor [resistance=68 package=THT]
  R201_3 = Resistor [resistance=68 package=THT]
  R201_4 = Resistor [resistance=68 package=THT]
  R201_5 = Resistor [resistance=68 package=THT]
  R201_6 = Resistor [resistance=68 package=THT]
  R201_7 = Resistor [resistance=68 package=THT]

nets:
  N1: DI1.cathodeE, R201.Pin_1
  N2: DI1.cathodeD, R201_2.Pin_1
  N3: DI1.commAnode#2, R201_3.Pin_1
  N4: DI1.cathodeB, R201_7.Pin_0
  N5: DI1.cathodeA, R201_6.Pin_0
  N6: DI1.cathodeF, R201_5.Pin_0
  N7: DI1.cathodeG, R201_4.Pin_0

notes:
  Description: Digital Meter
  Comment: Breadboard Layout
  Device: LED_METER
  File: 13.002.00.01.50.fz
  Revision: 20100213
  Author: Bert Timmerman
