# Fritzing sketch 26.006.00.01.50 (saved by Fritzing 0.3.14b)
breadboards: 2

parts:
  U201 = CA3140E_DIP08300
  U202 = CA3140E_DIP08300
  R201 = Resistor [resistance=12k package=THT]
  R202 = Resistor [resistance=2.2k package=THT]
  R203 = Resistor [resistance=2.2k package=THT]
  C201 = MKT Capacitor
  C202 = MKT Capacitor
  R205 = Resistor [resistance=120k package=THT]
  R206 = Resistor [resistance=22k package=THT]
  R204 = Trimmer Potentiometer [package=THT]
  C203 = Electrolytic Capacitor [package=THT]
  C204 = Ceramic Capacitor [package=THT]
  C205 = Ceramic Capacitor [package=THT]
  R207 = Resistor [resistance=10k package=THT]
  C206 = Ceramic Capacitor [package=THT]
  C207 = Ceramic Capacitor [package=THT]
  D201 = Signal Diode
  D202 = Signal Diode
  R208 = Resistor [resistance=15k package=THT]
  R209 = Resistor [resistance=1k package=THT]
  -15V_DC = Screw terminal - 2 pins [package=THT]
  +15V_DC = Screw terminal - 2 pins [package=THT]
  INPUT = Screw terminal - 2 pins [package=THT]
  GND = Screw terminal - 2 pins [package=THT]
  U203 = CA3140E_DIP08300
  C208 = Ceramic Capacitor [package=THT]
  C209 = Ceramic Capacitor [package=THT]
  OUTPUT = Screw terminal - 2 pins [package=THT]
  R211 = Trimmer Potentiometer [package=THT]
  D204 = Signal Diode
  RESET = Screw terminal - 2 pins [package=THT]
  D203 = Signal Diode
  R210 = Resistor [resistance=1M package=THT]
  FOLLOW = Screw terminal - 2 pins [package=THT]
  GND_2 = Screw terminal - 2 pins [package=THT]

nets:
  N1: U201.connector1, U202.connector1, R204.leg1, R204.wiper, C203.-, C204.pin_0, C205.pin_1, C206.pin_0, C207.pin_1, GND.pin1, GND.pin2, C208.pin_0, C209.pin_1, R211.leg1, GND_2.pin1, GND_2.pin2
  N2: U201.connector2, C202.connector1, R206.Pin_0
  N3: U201.connector3, U202.connector3, C204.pin_1, C206.pin_1, -15V_DC.pin1, -15V_DC.pin2, U203.connector3, C208.pin_1
  N4: U201.connector5, C201.connector1, R205.Pin_0, R207.Pin_1
  N5: U201.connector6, U202.connector6, C205.pin_0, C207.pin_0, +15V_DC.pin1, +15V_DC.pin2, U203.connector6, C209.pin_0
  N6: U202.connector0, D201.connector0, R208.Pin_0
  N7: U202.connector2, R207.Pin_0
  N8: U202.connector4, D201.connector1, D202.connector0
  N9: R201.Pin_0, INPUT.pin1, INPUT.pin2
  N10: R201.Pin_1, R202.Pin_1
  N11: R202.Pin_0, R203.Pin_0, C201.connector0, C202.connector0
  N12: R203.Pin_1, R204.leg2
  N13: R205.Pin_1, R206.Pin_1
  N14: C203.+, R209.Pin_1, U203.connector1, D204.connector1, R210.Pin_0
  N15: D202.connector1, R209.Pin_0
  N16: R208.Pin_1, U203.connector0, U203.connector4, R211.leg2
  N17: OUTPUT.pin1, OUTPUT.pin2, R211.wiper
  N18: D204.connector0, RESET.pin1, RESET.pin2
  N19: D203.connector0, R210.Pin_1
  N20: D203.connector1, FOLLOW.pin2

notes:
  Description: Octave Filter
  Comment: Breadboard Layout Band Pass Filter (31.5 Hz module)
  Device: OCTAVE_FILTER
  File: 26.006.00.01.50.fz
  Revision: 20100109
  Author: Bert Timmerman
